// Logisim project CPU_ALU.circ as structural Verilog: 1 circuit, main circuit CPU_ALU
module CPU_ALU (
  input  [3:0] Input_1,
  input  [3:0] Input_2,
  input  [3:0] FUNCTION_SELECT,
  output [3:0] RESULT,
  output [2:0] PZN_Positive_Zero_Negative
);

  wire [3:0] adder_1_out, adder_2_out, and_1_out, divider_1_out, divider_2_out, multiplier_1_out,
       negator_1_out, not_1_out, or_1_out, shifter_1_out, shifter_2_out, subtractor_1_out, undriven,
       undriven_2;

  assign not_1_out = ~Input_2;  // NOT_Gate not_1, 4 bits wide
  Adder #(.width(4)) adder_1 (.a(Input_2), .b(Input_1), .out(adder_1_out));  // open: cin, cout
  Subtractor #(.width(4)) subtractor_1 (.a(Input_2), .b(Input_1), .out(subtractor_1_out));  // open: bin, bout
  Multiplier #(.width(4)) multiplier_1 (.a(Input_2), .b(Input_1), .out(multiplier_1_out));  // open: cin, cout
  Divider #(.width(4)) divider_1 (.a(Input_2), .b(Input_1), .out(divider_1_out));  // open: upper, rem
  Negator #(.width(4)) negator_1 (.in(Input_2), .out(negator_1_out));
  Adder #(.width(4)) adder_2 (.a(not_1_out), .b(4'b1111), .out(adder_2_out));  // open: cin, cout
  Shifter #(.width(4)) shifter_1 (.in(Input_2), .\dist (2'b11), .out(shifter_1_out));
  Shifter #(.width(4), .shift("lr")) shifter_2 (.in(Input_2), .\dist (2'b11), .out(shifter_2_out));
  Shifter #(.width(4), .shift("ar")) shifter_3 (.in(Input_2), .\dist (2'b11), .out(shifter_2_out));
  assign and_1_out = Input_2 & Input_1;  // AND_Gate and_1, 4 bits wide
  assign or_1_out = Input_2 | Input_1;  // OR_Gate or_1, 4 bits wide
  Multiplexer #(.select(4), .width(4), .enable("false")) multiplexer_1 (
    .in0(4'b0000), .in1(4'b1111), .in2(Input_1), .in3(Input_2), .in4(adder_1_out), .in5(subtractor_1_out),
    .in6(multiplier_1_out), .in7(divider_1_out), .in8(negator_1_out), .in9(and_1_out), .in10(or_1_out),
    .in11(adder_2_out), .in12(shifter_1_out), .in13(shifter_2_out), .in14(shifter_2_out),
    .out({PZN_Positive_Zero_Negative[0], RESULT[2:0]}), .sel(FUNCTION_SELECT));  // open: in15
  Divider #(.width(4)) divider_2 (.a(undriven), .b(undriven_2), .out(divider_2_out));  // open: upper, rem
  and and_2 (PZN_Positive_Zero_Negative[1], ~RESULT[0], ~RESULT[1], ~RESULT[2], ~PZN_Positive_Zero_Negative[0]);  // AND_Gate
  and and_3 (PZN_Positive_Zero_Negative[2], ~PZN_Positive_Zero_Negative[1], ~PZN_Positive_Zero_Negative[0]);  // AND_Gate

  assign RESULT[3] = PZN_Positive_Zero_Negative[0];
endmodule
