// Logisim project Register_ALU_Datapath.circ as structural Verilog: 3 circuits, main circuit REGISTER_FILE
module REGISTER_FILE (
  input  [3:0] DATAIN,
  input  LOAD,
  input  [2:0] address_A,
  input  [2:0] address_B,
  input  CLK,
  input  [2:0] DATA_ADDRESS,
  output [3:0] adress_A_out,
  output [3:0] adress_B_out
);

  wire and_1_out, and_2_out, and_3_out, and_4_out, and_5_out, and_6_out, and_7_out, and_8_out,
       decoder_1_out0, decoder_1_out1, decoder_1_out2, decoder_1_out3, decoder_1_out4, decoder_1_out5,
       decoder_1_out6, decoder_1_out7;
  wire [3:0] register_1_q, register_2_q, register_3_q, register_4_q, register_5_q, register_6_q,
       register_7_q, register_8_q;

  Decoder #(.select(3)) decoder_1 (
    .out0(decoder_1_out0), .out1(decoder_1_out1), .out2(decoder_1_out2), .out3(decoder_1_out3),
    .out4(decoder_1_out4), .out5(decoder_1_out5), .out6(decoder_1_out6), .out7(decoder_1_out7),
    .sel(DATA_ADDRESS));  // open: en
  and and_1 (and_1_out, LOAD, decoder_1_out0);
  and and_2 (and_2_out, LOAD, decoder_1_out1);
  and and_3 (and_3_out, LOAD, decoder_1_out2);
  and and_4 (and_4_out, LOAD, decoder_1_out3);
  Register #(.width(4)) register_1 (.D(DATAIN), .en(and_1_out), .Q(register_1_q), .clk(CLK), .clr(1'b0));
  Register #(.width(4)) register_2 (.D(DATAIN), .en(and_2_out), .Q(register_2_q), .clk(CLK), .clr(1'b0));
  Register #(.width(4)) register_3 (.D(DATAIN), .en(and_3_out), .Q(register_3_q), .clk(CLK), .clr(1'b0));
  Register #(.width(4)) register_4 (.D(DATAIN), .en(and_4_out), .Q(register_4_q), .clk(CLK), .clr(1'b0));
  and and_5 (and_5_out, LOAD, decoder_1_out4);
  and and_6 (and_6_out, LOAD, decoder_1_out5);
  and and_7 (and_7_out, LOAD, decoder_1_out6);
  and and_8 (and_8_out, LOAD, decoder_1_out7);
  Register #(.width(4)) register_5 (.D(DATAIN), .en(and_5_out), .Q(register_5_q), .clk(CLK), .clr(1'b0));
  Register #(.width(4)) register_6 (.D(DATAIN), .en(and_6_out), .Q(register_6_q), .clk(CLK), .clr(1'b0));
  Register #(.width(4)) register_7 (.D(DATAIN), .en(and_7_out), .Q(register_7_q), .clk(CLK), .clr(1'b0));
  Register #(.width(4)) register_8 (.D(DATAIN), .en(and_8_out), .Q(register_8_q), .clk(CLK), .clr(1'b0));
  Multiplexer #(.select(3), .width(4)) multiplexer_1 (
    .in0(register_1_q), .in1(register_2_q), .in2(register_3_q), .in3(register_4_q), .in4(register_5_q),
    .in5(register_6_q), .in6(register_7_q), .in7(register_8_q), .out(adress_B_out), .sel(address_B));  // open: en
  Multiplexer #(.select(3), .width(4)) multiplexer_2 (
    .in0(register_1_q), .in1(register_2_q), .in2(register_3_q), .in3(register_4_q), .in4(register_5_q),
    .in5(register_6_q), .in6(register_7_q), .in7(register_8_q), .out(adress_A_out), .sel(address_A));  // open: en
endmodule

module CPU_ALU (
  input  [3:0] Input_1,
  input  [3:0] Input_2,
  input  [3:0] FUNCTION_SELECT,
  output [3:0] RESULT,
  output [2:0] PZN_Positive_Zero_Negative
);

  wire [3:0] adder_1_out, adder_2_out, and_1_out, divider_1_out, divider_2_out, multiplier_1_out,
       negator_1_out, not_1_out, or_1_out, shifter_1_out, shifter_2_out, subtractor_1_out, undriven,
       undriven_2;

  assign not_1_out = ~Input_2;  // NOT_Gate not_1, 4 bits wide
  Adder #(.width(4)) adder_1 (.a(Input_2), .b(Input_1), .out(adder_1_out));  // open: cin, cout
  Subtractor #(.width(4)) subtractor_1 (.a(Input_2), .b(Input_1), .out(subtractor_1_out));  // open: bin, bout
  Multiplier #(.width(4)) multiplier_1 (.a(Input_2), .b(Input_1), .out(multiplier_1_out));  // open: cin, cout
  Divider #(.width(4)) divider_1 (.a(Input_2), .b(Input_1), .out(divider_1_out));  // open: upper, rem
  Negator #(.width(4)) negator_1 (.in(Input_2), .out(negator_1_out));
  Adder #(.width(4)) adder_2 (.a(not_1_out), .b(4'b1111), .out(adder_2_out));  // open: cin, cout
  Shifter #(.width(4)) shifter_1 (.in(Input_2), .\dist (2'b11), .out(shifter_1_out));
  Shifter #(.width(4), .shift("lr")) shifter_2 (.in(Input_2), .\dist (2'b11), .out(shifter_2_out));
  Shifter #(.width(4), .shift("ar")) shifter_3 (.in(Input_2), .\dist (2'b11), .out(shifter_2_out));
  assign and_1_out = Input_2 & Input_1;  // AND_Gate and_1, 4 bits wide
  assign or_1_out = Input_2 | Input_1;  // OR_Gate or_1, 4 bits wide
  Multiplexer #(.select(4), .width(4), .enable("false")) multiplexer_1 (
    .in0(4'b0000), .in1(4'b1111), .in2(Input_1), .in3(Input_2), .in4(adder_1_out), .in5(subtractor_1_out),
    .in6(multiplier_1_out), .in7(divider_1_out), .in8(negator_1_out), .in9(and_1_out), .in10(or_1_out),
    .in11(adder_2_out), .in12(shifter_1_out), .in13(shifter_2_out), .in14(shifter_2_out),
    .out({PZN_Positive_Zero_Negative[0], RESULT[2:0]}), .sel(FUNCTION_SELECT));  // open: in15
  Divider #(.width(4)) divider_2 (.a(undriven), .b(undriven_2), .out(divider_2_out));  // open: upper, rem
  and and_2 (PZN_Positive_Zero_Negative[1], ~RESULT[0], ~RESULT[1], ~RESULT[2], ~PZN_Positive_Zero_Negative[0]);  // AND_Gate
  and and_3 (PZN_Positive_Zero_Negative[2], ~PZN_Positive_Zero_Negative[1], ~PZN_Positive_Zero_Negative[0]);  // AND_Gate

  assign RESULT[3] = PZN_Positive_Zero_Negative[0];
endmodule

module DATA_PATH (
  input  [2:0] Destination,
  input  Register_Write,
  input  [2:0] Address_A,
  input  [2:0] Address_B,
  input  [3:0] ConstantIN,
  input  MUX_B,
  input  CLK,
  input  [3:0] Function_Select,
  input  [3:0] Data_In,
  input  MUX_A,
  output [2:0] PZN,
  output [3:0] out_12
);

  wire [3:0] multiplexer_1_out, multiplexer_2_out, register_file_1_adress_a_out, register_file_1_adress_b_out;

  REGISTER_FILE register_file_1 (
    .DATAIN(multiplexer_2_out), .LOAD(Register_Write), .CLK(CLK),
    .adress_A_out(register_file_1_adress_a_out), .adress_B_out(register_file_1_adress_b_out),
    .DATA_ADDRESS(Destination), .address_A(Address_A), .address_B(Address_B));
  Multiplexer #(.width(4), .enable("false")) multiplexer_1 (
    .in0(register_file_1_adress_b_out), .in1(ConstantIN), .out(multiplexer_1_out), .sel(MUX_B));
  CPU_ALU cpu_alu_1 (
    .Input_1(register_file_1_adress_a_out), .Input_2(multiplexer_1_out), .RESULT(out_12),
    .PZN_Positive_Zero_Negative(PZN), .FUNCTION_SELECT(Function_Select));
  Multiplexer #(.width(4), .enable("false")) multiplexer_2 (
    .in0(out_12), .in1(Data_In), .out(multiplexer_2_out), .sel(MUX_A));
endmodule
